// Digital circuit P63.dig as structural Verilog
module P63 (
  input  clk,
  input  rst,
  input  push,
  input  pop,
  input  [3:0] d,
  output [3:0] top,
  output [2:0] count,
  output empty,
  output full
);

  wire and_1_out, and_2_out, and_5_out, and_6_out, and_7_out, and_8_out, and_10_out, and_11_out,
       decoder_1_out_0, decoder_1_out_1, decoder_1_out_2, multiplexer_6_out, multiplexer_7_out,
       multiplexer_8_out, multiplexer_9_out, multiplexer_10_out, multiplexer_12_out, multiplexer_13_out,
       not_1_out, not_2_out, not_3_out, not_4_out, not_5_out, or_1_out, undriven, undriven_2, xor_1_out,
       xor_2_out;
  wire [3:0] and_9_out, d_ff_1_q, d_ff_3_q, multiplexer_1_out, multiplexer_2_out, multiplexer_3_out,
       multiplexer_4_out, multiplexer_5_out;

  not not_1 (not_1_out, pop);
  not not_2 (not_2_out, push);
  and and_1 (and_1_out, push, not_1_out);
  and and_2 (and_2_out, pop, not_2_out);
  // NOr nor_1 has open pins: In_1=count[0], In_2=count[1], out=open
  not not_3 (not_3_out, undriven_2);
  Decoder #(.Selector_Bits(2)) decoder_1 (
    .out_0(decoder_1_out_0), .out_1(decoder_1_out_1), .out_2(decoder_1_out_2), .out_3(decoder_1_out_1));  // open: sel
  and and_3 (empty, undriven, not_3_out);
  and and_4 (full, undriven, undriven_2);
  and and_5 (and_5_out, decoder_1_out_0, d_ff_1_q[0]);
  and and_6 (and_6_out, decoder_1_out_1, and_9_out[0]);
  and and_7 (and_7_out, decoder_1_out_2, d_ff_3_q[0]);
  and and_8 (and_8_out, decoder_1_out_1, and_9_out[0]);
  not not_4 (not_4_out, full);
  not not_5 (not_5_out, empty);
  Multiplexer #(.Bits(4)) multiplexer_1 (.sel(and_5_out), .in_0(d_ff_1_q), .in_1(and_9_out), .out(multiplexer_1_out));
  Multiplexer #(.Bits(4)) multiplexer_2 (.sel(and_6_out), .in_0(and_9_out), .in_1(d_ff_3_q), .out(multiplexer_2_out));
  Multiplexer #(.Bits(4)) multiplexer_3 (.sel(and_7_out), .in_0(d_ff_3_q), .in_1(and_9_out), .out(multiplexer_3_out));
  Multiplexer #(.Bits(4)) multiplexer_4 (.sel(and_8_out), .in_0(and_9_out), .out(multiplexer_4_out));  // open: in_1
  and and_9 (and_9_out[0], and_1_out, not_4_out);
  and and_10 (and_10_out, and_2_out, not_5_out);
  D_FF #(.Bits(4)) d_ff_1 (.D(multiplexer_1_out), .C(clk), .Q(d_ff_1_q));  // open: nQ
  D_FF #(.Bits(4)) d_ff_2 (.D(multiplexer_2_out), .C(clk), .Q(and_9_out));  // open: nQ
  D_FF #(.Bits(4)) d_ff_3 (.D(multiplexer_3_out), .C(clk), .Q(d_ff_3_q));  // open: nQ
  D_FF #(.Bits(4)) d_ff_4 (.D(multiplexer_4_out), .C(clk), .Q(and_9_out));  // open: nQ
  xor xor_1 (xor_1_out, count[0], or_1_out);
  or or_1 (or_1_out, and_9_out[0], and_10_out);
  xor xor_2 (xor_2_out, count[1], count[0]);
  and and_11 (and_11_out, count[1], count[0]);
  Multiplexer #(.Bits(4), .Selector_Bits(2)) multiplexer_5 (
    .sel(count[1:0]), .in_0(4'b0000), .in_1(d_ff_1_q), .in_2(and_9_out), .in_3(d_ff_3_q),
    .out(multiplexer_5_out));
  Multiplexer #(.Bits(1)) multiplexer_6 (.sel(rst), .in_0(xor_1_out), .out(multiplexer_6_out));  // open: in_1
  Multiplexer #(.Bits(1)) multiplexer_7 (.sel(and_10_out), .in_0(count[1]), .out(multiplexer_7_out));  // open: in_1
  Multiplexer #(.Bits(1)) multiplexer_8 (
    .sel(and_9_out[0]), .in_0(multiplexer_7_out), .out(multiplexer_8_out));  // open: in_1
  or or_2 (multiplexer_7_out, undriven_2, and_11_out);
  Multiplexer #(.Bits(1)) multiplexer_9 (.sel(and_10_out), .in_0(undriven_2), .out(multiplexer_9_out));  // open: in_1
  Multiplexer #(.Bits(1)) multiplexer_10 (
    .sel(and_9_out[0]), .in_0(multiplexer_9_out), .out(multiplexer_10_out));  // open: in_1
  Multiplexer #(.Bits(4)) multiplexer_11 (.sel(count[2]), .in_0(multiplexer_5_out), .out(top));  // open: in_1
  D_FF #(.Bits(1)) d_ff_5 (.D(multiplexer_6_out), .C(clk), .Q(count[0]));  // open: nQ
  Multiplexer #(.Bits(1)) multiplexer_12 (.sel(rst), .in_0(multiplexer_8_out), .out(multiplexer_12_out));  // open: in_1
  Multiplexer #(.Bits(1)) multiplexer_13 (
    .sel(rst), .in_0(multiplexer_10_out), .out(multiplexer_13_out));  // open: in_1
  D_FF #(.Bits(1)) d_ff_6 (.D(multiplexer_12_out), .C(clk), .nQ(count[1]));  // open: Q
  D_FF #(.Bits(1)) d_ff_7 (.D(multiplexer_13_out), .C(clk), .Q(count[2]));  // open: nQ
  // Pins of 1 and 4 bits meet at and_9_out
  // Pins of 1 and 4 bits meet at d_ff_1_q
  // Pins of 1 and 4 bits meet at d_ff_3_q
  // also tied to GND on the sheet: and_9_out[0]

  // Notes on the sheet:
  //   clk: Hz: 1
  //   P63 Hardware stack - Digital task
  //   4 entries x 4 bits with a stack pointer.
  //   Allowed parts: gates + multiplexer/decoder parts + flip-flops
  //   Do not rename, move or delete the input and output pins.
endmodule

/* Test case public tests:
clk rst push pop d top count empty full
C 1 0 0 1 0 0 1 0
C 0 0 1 15 0 0 1 0
C 0 1 0 7 7 1 0 0
C 0 1 0 15 15 2 0 0
C 1 0 1 3 0 0 1 0
C 0 1 1 6 0 0 1 0
C 1 0 1 3 0 0 1 0
C 0 1 0 2 2 1 0 0
C 0 0 0 0 2 1 0 0
C 0 1 1 3 2 1 0 0
C 0 0 1 9 0 0 1 0
C 0 1 1 15 0 0 1 0
C 0 1 0 12 12 1 0 0
C 0 0 0 13 12 1 0 0
C 0 1 0 11 11 2 0 0
C 0 0 0 8 11 2 0 0
C 0 1 0 6 6 3 0 0
C 0 0 1 10 11 2 0 0
C 0 0 0 3 11 2 0 0
C 0 0 0 2 11 2 0 0
C 0 1 1 15 11 2 0 0
C 0 0 1 7 12 1 0 0
C 0 0 0 5 12 1 0 0
C 0 1 1 8 12 1 0 0
C 0 1 1 5 12 1 0 0
C 0 1 1 13 12 1 0 0
C 0 0 1 12 0 0 1 0
C 0 0 0 12 0 0 1 0
C 0 0 0 15 0 0 1 0
C 0 0 0 15 0 0 1 0
C 0 0 0 15 0 0 1 0
C 0 0 1 7 0 0 1 0
C 0 0 0 3 0 0 1 0
C 0 1 0 0 0 1 0 0
C 1 0 1 0 0 0 1 0
C 0 1 0 11 11 1 0 0
C 0 0 1 10 0 0 1 0
C 0 0 1 2 0 0 1 0
C 0 0 1 11 0 0 1 0
C 0 1 0 12 12 1 0 0
C 0 0 1 14 0 0 1 0
C 0 0 0 10 0 0 1 0
C 0 1 1 11 0 0 1 0
C 0 1 1 15 0 0 1 0
C 0 1 1 5 0 0 1 0
C 0 1 1 4 0 0 1 0
C 0 1 1 15 0 0 1 0
C 0 1 0 7 7 1 0 0
C 0 0 1 10 0 0 1 0
C 0 0 0 5 0 0 1 0
C 0 1 1 14 0 0 1 0
C 0 1 0 4 4 1 0 0
C 0 0 0 6 4 1 0 0
C 0 1 1 7 4 1 0 0
C 0 0 0 4 4 1 0 0
C 0 1 0 12 12 2 0 0
C 0 1 0 14 14 3 0 0
C 0 0 0 1 14 3 0 0
C 0 0 0 10 14 3 0 0
C 0 1 1 5 14 3 0 0
C 0 0 1 15 12 2 0 0
C 0 0 0 4 12 2 0 0
C 0 1 1 11 12 2 0 0
C 0 1 0 1 1 3 0 0
C 0 1 1 7 1 3 0 0
C 0 0 1 1 12 2 0 0
C 0 0 1 7 4 1 0 0
C 0 0 0 5 4 1 0 0
C 0 0 0 0 4 1 0 0
C 0 0 1 3 0 0 1 0
C 0 0 0 4 0 0 1 0
C 0 1 1 13 0 0 1 0
C 0 0 1 8 0 0 1 0
C 1 1 1 8 0 0 1 0
C 0 1 0 15 15 1 0 0
C 0 0 0 5 15 1 0 0
C 0 0 1 6 0 0 1 0
C 0 1 1 13 0 0 1 0
C 0 0 0 9 0 0 1 0
C 0 0 1 11 0 0 1 0
C 0 1 1 10 0 0 1 0
C 0 1 0 11 11 1 0 0
C 0 1 1 11 11 1 0 0
C 0 1 1 8 11 1 0 0
C 0 1 0 14 14 2 0 0
C 0 1 1 6 14 2 0 0
C 0 0 1 7 11 1 0 0
C 0 0 0 6 11 1 0 0
C 0 0 0 8 11 1 0 0
C 0 1 0 0 0 2 0 0
C 0 1 0 0 0 3 0 0
C 0 1 0 12 12 4 0 1
C 0 1 1 4 12 4 0 1
C 0 1 0 9 12 4 0 1
C 0 1 0 2 12 4 0 1
C 0 0 0 11 12 4 0 1
C 0 1 0 1 12 4 0 1
C 0 1 0 3 12 4 0 1
C 0 1 1 3 12 4 0 1
C 0 0 1 9 0 3 0 0
C 0 0 1 10 0 2 0 0
C 0 0 0 14 0 2 0 0
C 0 1 0 9 9 3 0 0
C 0 0 0 7 9 3 0 0
C 0 1 1 11 9 3 0 0
C 0 1 0 0 0 4 0 1
C 0 0 1 1 9 3 0 0
C 0 0 1 8 0 2 0 0
C 0 1 1 0 0 2 0 0
C 0 1 0 8 8 3 0 0
C 0 0 0 13 8 3 0 0
C 0 0 1 15 0 2 0 0
C 0 1 0 2 2 3 0 0
C 0 0 0 5 2 3 0 0
C 0 0 0 7 2 3 0 0
C 0 1 1 0 2 3 0 0
C 0 1 1 15 2 3 0 0
C 0 1 0 15 15 4 0 1
C 0 0 1 0 2 3 0 0
C 0 1 0 1 1 4 0 1
C 0 0 1 7 2 3 0 0
C 0 1 1 15 2 3 0 0
C 0 0 0 7 2 3 0 0
C 0 0 0 2 2 3 0 0
C 0 1 1 7 2 3 0 0
C 0 0 1 13 0 2 0 0
C 0 0 0 0 0 2 0 0
C 0 0 0 0 0 2 0 0
C 0 1 1 7 0 2 0 0
C 0 0 1 7 11 1 0 0
C 0 1 0 2 2 2 0 0
C 0 0 0 15 2 2 0 0
C 0 1 1 7 2 2 0 0
C 0 1 1 14 2 2 0 0
C 0 1 1 11 2 2 0 0
C 0 0 0 2 2 2 0 0
C 0 0 0 11 2 2 0 0
C 0 1 1 15 2 2 0 0
C 0 1 0 6 6 3 0 0
C 0 1 1 4 6 3 0 0
C 0 1 0 8 8 4 0 1
C 0 0 0 8 8 4 0 1
C 0 1 0 13 8 4 0 1
C 0 1 0 6 8 4 0 1
C 0 0 0 3 8 4 0 1
C 0 0 0 13 8 4 0 1
C 0 0 1 7 6 3 0 0
C 0 1 0 7 7 4 0 1
C 0 1 1 7 7 4 0 1
C 0 1 1 0 7 4 0 1
C 0 0 0 0 7 4 0 1
C 0 1 1 4 7 4 0 1
C 0 0 1 14 6 3 0 0
C 0 0 0 13 6 3 0 0
C 0 0 1 0 2 2 0 0
C 0 1 0 13 13 3 0 0
C 0 0 0 13 13 3 0 0
C 0 0 0 6 13 3 0 0
C 0 1 0 8 8 4 0 1
C 0 0 0 7 8 4 0 1
*/
